# Fritzing sketch TumblerController (saved by Fritzing 0.9.3b)
circuit board: 14.4604cm x 9.61509cm
breadboards: 1

parts:
  Pro_Micro1 = Pro Micro
  R1 = Resistor [tolerance=±5% resistance=470 package=THT]
  R2 = Resistor [tolerance=±5% resistance=1k package=THT]
  LM1 = LM741 [part_number=LM741 package="DIP (Dual Inline) [THT]"]
  R3 = Resistor [tolerance=±5% resistance=470 package=THT]
  C1 = Capacitor Polarized [package=cpol-radial-100uf-25v]
  F1 = FUSE [package=fuse_5mm]
  IC1 = Voltage Regulator [package=78xxl]
  U1 = Voltage Regulator [package=to220-adj]
  J1 = Power Jack [package=power_jack_slot]
  Grove1 = Grove 4 Digit Display
  R4 = Resistor [tolerance=±5% resistance=330 package=THT]
  U2 = RELAY [package=relay-t9a-2]
  M1 = DC Motor
  S1 = Momentary Switch [package=tactile-pth]

nets:
  N1: Pro_Micro1.D2, Grove1.CLK
  N2: Pro_Micro1.D3, Grove1.DIO
  N3: Pro_Micro1.D5, S1.1
  N4: Pro_Micro1.D6, R1.Pin_1
  N5: Pro_Micro1.D16/MOSI, U2.COIL2
  VCC: Pro_Micro1.VCC, IC1.OUT, Grove1.VCC
  GND: Pro_Micro1.GND, LM1.pin4, R3.Pin_0, C1.-, IC1.GND, J1.GND, Grove1.GND, U2.COIL1, M1.pin_2, S1.4
  N6: R1.Pin_0, LM1.pin3, C1.+
  N7: R2.Pin_0, LM1.pin2, R3.Pin_1
  N8: R2.Pin_1, LM1.pin6, U1.ADJ, R4.Pin_1
  N9: LM1.pin7, F1.2, IC1.IN, U1.IN
  N10: F1.1, J1.PWR
  N11: U1.OUT, R4.Pin_0, U2.MAIN
  N12: U2.NO, M1.pin_1

notes:
  Motor Controller for a Tumbler

custom parts:
  Pro Micro: The SparkFun Pro Micro is a complete USB-based microcontoller development system, in a very small footprint, capable of implementing many types of projects. All programming can be done via the USB port.
  LM741: This is a single Op Amp DIP.

// code stored in the sketch: TumblerController.h.ino
/**********************************
*                                                        *
*    Tumbler Motor Controller                *
*                                                       *
*        By Alon Fliess                            *
*                                                       *
*            2019                                    *
*                                                        *
/*********************************/

#ifndef _TUMBLER_CONTROLLER_H
#define _TUMBLER_CONTROLLER_H
// Module connection pins (Digital Pins)
#define CLK 2
#define DIO 3
#define SPD 6
#define BUTTON 5
#define RELAY 16

// The amount of time (in milliseconds) that a button action is conssidered
const unsigned int minimumButtonPressingTime = 75;
const unsigned int LongPressTime = 200;

const uint8_t SEG_DONE[] = {
  SEG_B | SEG_C | SEG_D | SEG_E | SEG_G,           // d
  SEG_A | SEG_B | SEG_C | SEG_D | SEG_E | SEG_F,   // O
  SEG_C | SEG_E | SEG_G,                           // n
  SEG_A | SEG_D | SEG_E | SEG_F | SEG_G            // E
  };

  const uint8_t SEG_START[] = {
  SEG_A | SEG_F | SEG_G | SEG_C | SEG_D,           // S
  SEG_B | SEG_G | SEG_C ,                          // t
  SEG_E | SEG_G,                                   // r
  SEG_B | SEG_G | SEG_C                            // t
  };

  const uint8_t SEG_STOP[] = {
  SEG_A | SEG_F | SEG_G | SEG_C | SEG_D,           // S
  SEG_B | SEG_G | SEG_C ,                          // t
  SEG_A | SEG_B | SEG_C | SEG_D | SEG_E | SEG_F,   // O
  SEG_A | SEG_F | SEG_G | SEG_B | SEG_E            // p
  };

  const uint8_t SEG_SPD[] = {
  0,                                               // _
  SEG_A | SEG_F | SEG_G | SEG_C | SEG_D,           // S
  SEG_A | SEG_F | SEG_G | SEG_B | SEG_E,           // p
  SEG_B | SEG_C | SEG_D | SEG_E | SEG_G            // d
  };

  const uint8_t SEG_SPD_DOWN[] = {
  SEG_G,                                           // -
  SEG_A | SEG_F | SEG_G | SEG_C | SEG_D,           // S
  SEG_A | SEG_F | SEG_G | SEG_B | SEG_E,           // p
  SEG_B | SEG_C | SEG_D | SEG_E | SEG_G            // d
  };

  const uint8_t SEG_DUR[] = {
  0,                                               // _
  SEG_B | SEG_C | SEG_D | SEG_E | SEG_G,           // d
  SEG_F | SEG_E | SEG_D | SEG_C | SEG_B,           // U
  SEG_E | SEG_G                                    // r
  };

  const uint8_t SEG_DUR_DOWN[] = {
  SEG_G,                                           // -
  SEG_B | SEG_C | SEG_D | SEG_E | SEG_G,           // d
  SEG_F | SEG_E | SEG_D | SEG_C | SEG_B,           // U
  SEG_E | SEG_G                                    // r
  };

  const uint8_t SEG_RESET[] = {
  SEG_E | SEG_G,                                   // r
  SEG_A | SEG_D | SEG_E | SEG_F | SEG_G,           // E
  SEG_A | SEG_F | SEG_G | SEG_C | SEG_D,           // S
  SEG_B | SEG_G | SEG_C                            // t
  };

const uint8_t PERIMETER[] = {4, 5, 0, 10, 20, 30, 31, 32, 33, 23, 13, 3};

typedef void (*func_t)();
class Action
{
  private:
  const uint8_t* _display;
  func_t _func;
  
  public:
  Action(const uint8_t* display, func_t func)
    : _display(display), _func(func) {}
  void Display();
  void Act();
};

enum ButtonAction {ButtonActionNone, ButtonActionShortPress, ButtonActionLongPress};

ButtonAction DetectButtonAction();

#endif //_TUMBLER_CONTROLLER_H

// code stored in the sketch: TumblerController.ino
/**********************************
*                                                        *
*    Tumbler Motor Controller                *
*                                                       *
*        By Alon Fliess                            *
*                                                       *
*            2019                                    *
*                                                        *
/*********************************/

#include <Arduino.h>
#include <TM1637Display.h>
#include "TumblerController.h"

TM1637Display display(CLK, DIO);
unsigned int speed = 3;
unsigned int time = 24 * 60; //in minutes
bool isRunning = false;
unsigned long lastAccountingTime;
unsigned long pressTime;
unsigned long buttonPressStartTime;
bool buttonPreviousState = false;
unsigned long lastActionTime = 0;
unsigned char currentAction = 0;

Action actions[] = {Action(SEG_START, &Start), 
                    Action(SEG_SPD, &SpeedUp), Action(SEG_SPD_DOWN, &SpeedDown),
                    Action(SEG_DUR, &TimeUp), Action(SEG_DUR_DOWN, &TimeDown),
                    Action(SEG_RESET, &Reset)
};

void DisplayRunningLoop(int times, int stepDelay)
{
  int length = sizeof(PERIMETER)/sizeof(PERIMETER[0]);
  for (int t = 0; t < times; ++t) //times
  {
    for (int loop = 0; loop < length; ++loop)
    {
      uint8_t LEDS[] = {0,0,0,0};
      for (int digit = 0; digit < length/2; ++digit)
      {
        int shiftedDigit = (digit + loop)%length;
        int index = PERIMETER[shiftedDigit] / 10;
        int led = 1 << (PERIMETER[shiftedDigit] % 10);
        LEDS[index] |= led;
      }
      display.setSegments(LEDS);
      delay(stepDelay);
    }
  }
}

void Start()
{
  isRunning = true;
  analogWrite(SPD, 75 + (speed - 1) * 30);
  delay(250);
  digitalWrite(RELAY, LOW);
  lastAccountingTime = millis();
}

void Stop()
{
  digitalWrite(RELAY, HIGH);
  digitalWrite(SPD, 0);
  isRunning = false;
  currentAction = 0; 
  DisplayRunningLoop(2, 4);
  display.clear();
  display.setSegments(SEG_STOP);
  delay(400);
  actions[currentAction].Display();
  lastActionTime = millis();  
}

void DisplaySpeed(bool shouldErase = true)
{
  if (shouldErase)
    display.clear();
  display.showNumberDec(speed, false); 
}

void SpeedUp()
{
  ++speed;
  if (speed > 5)
    speed = 5;
  DisplaySpeed();
}

void SpeedDown()
{
  --speed;
  if (speed < 1)
    speed = 1;
  DisplaySpeed();
}

void DisplayTime(bool shouldErase = true, uint8_t colon = 0b01000000)
{
  auto hours = time / 60;
  auto minutes = time % 60;
  if (shouldErase)
    display.clear();
  display.showNumberDecEx(minutes + hours * 100, colon, true);
}
void TimeUp()
{
  time += 30;
  DisplayTime();
}

void TimeDown()
{
  if (time == 0)
  return;
  
  if (time < 30)
  {
    --time;
    DisplayTime();
    return;
  }
  
  time -= 30;
  DisplayTime();
}

void Reset()
{
  speed = 3;
  isRunning = false;
  time = 24 * 60;
  DisplayRunningLoop(4, 2);
  currentAction = 0; 
  actions[currentAction].Display();
  lastActionTime = millis();
}

void Action::Display()
{
  display.clear();
  display.setSegments(_display);
}

void Action::Act()
{
  _func();
}


ButtonAction DetectButtonAction()
{
  bool current = digitalRead(BUTTON) == 0; //pull up
  if (!current && buttonPreviousState && (millis() - pressTime) > LongPressTime)
  {
    buttonPreviousState = false;
    Serial.println("ButtonActionLongPress");
    return ButtonActionLongPress;
  }
  //else
  if (!current && buttonPreviousState && (millis() - pressTime) > minimumButtonPressingTime)
  {
    buttonPreviousState = false;
    Serial.println("ButtonActionShortPress");
    return ButtonActionShortPress;
  }

  if (current && !buttonPreviousState)
  {
    pressTime = millis();
  }
  buttonPreviousState = current;
  return ButtonActionNone;
}

void setup()
{
  pinMode(SPD, OUTPUT);
  pinMode(BUTTON, INPUT_PULLUP); 
  digitalWrite(RELAY, HIGH);
  pinMode(RELAY, OUTPUT); 
  
 //blink 5 times
  display.clear();
  uint8_t data[] = { 0xff, 0xff, 0xff, 0xff };
  uint8_t blank[] = { 0x00, 0x00, 0x00, 0x00 };
  for (int i = 0; i < 5; ++i)
  {
    display.setBrightness(0x0f - 4 + i);
    display.setSegments(data);
    delay(25);
    display.setSegments(blank);
    delay(25);
  }
  display.clear();
  DisplayRunningLoop(4, 7);
  display.setSegments(SEG_START);
  Serial.begin(9600);
}

auto clockColon = 0b01000000;
byte lastSecondDigit = 0;
void HandleRunning(ButtonAction buttonAction)
{
  if (buttonAction != ButtonActionNone)
  {
    Stop();
    return;
  }
  bool shouldErase = false;
  if (millis() - lastAccountingTime >= 60000) //a minute
  {
    lastAccountingTime = millis();
    time -= 1;
    shouldErase = true;
  }

  byte secondDigit = (millis() / 1000)%10;
  if (secondDigit != lastSecondDigit) //a second has passed
  {
    lastSecondDigit = secondDigit;
    clockColon = (clockColon == 0b01000000) ? 0 : 0b01000000;
  }
  DisplayTime(shouldErase, clockColon);
  if (time == 0)
      Stop();
}

void ShowStatus()
{
    if ((millis() / 1000) % 2 == 1)
    {
      DisplayTime(false);
    }
    else
    {
      DisplaySpeed(false);
    }
}

void loop()
{
  if (millis() - lastActionTime > 5 * 60 * 1000)
    display.setBrightness(0);
    
  auto buttonAction = DetectButtonAction();
  if (isRunning)
  {
    HandleRunning(buttonAction);
    return;
  }
  //else
  display.setBrightness(0xf);
  //not running, handle menue
  if (buttonAction == ButtonActionLongPress)
  {
    currentAction = (currentAction + 1) % (sizeof(actions)/sizeof(actions[0]));
    actions[currentAction].Display();
    lastActionTime = millis();
    return;
  }
  //else
  if (buttonAction == ButtonActionShortPress)
  {
    actions[currentAction].Act();
    lastActionTime = millis();
  }

  if (millis() - lastActionTime > 10 * 1000)
  {
     ShowStatus();
  }
}
