# Fritzing sketch TumblerController_new (saved by Fritzing 0.9.3b)
stripboards: 1

parts:
  Pro_Micro2 = Pro Micro
  IC2 = Voltage Regulator [package=78xxl]
  F2 = FUSE [package=fuse_5mm]
  J1 = Camdenboss CTB0158-2 [part_number=CTB0158-2 package=THT]
  J2 = Camdenboss CTB0158-4 [part_number=CTB0158-4 package=THT]
  J3 = Camdenboss CTB0158-2 [part_number=CTB0158-2 package=THT]
  J4 = Camdenboss CTB0158-2 [part_number=CTB0158-2 package=THT]
  Grove2 = Grove 4 Digit Display
  S2 = Momentary Switch [package=tactile-pth]
  LM2 = LM741 [part_number=LM741 package="DIP (Dual Inline) [THT]"]
  R2 = Resistor [tolerance=±5% resistance=470 package=THT]
  C2 = Capacitor Polarized [package=cpol-radial-100uf-25v]
  R4 = Resistor [tolerance=±5% resistance=470 package=THT]
  R5 = Resistor [tolerance=±5% resistance=1k package=THT]
  J5 = Camdenboss CTB0158-5 [part_number=CTB0158-5 package=THT]
  M2 = DC Motor
  R6 = Resistor [tolerance=±5% resistance=330 package=THT]
  KY-2 = Keyes Relay [package=THT]
  U3 = Voltage Regulator [package=to220-adj]

nets:
  N1: Pro_Micro2.D2, J2.pin4
  N2: Pro_Micro2.D3, J2.pin3
  N3: Pro_Micro2.D5, J3.pin2
  N4: Pro_Micro2.D6, R2.Pin_1
  N5: Pro_Micro2.D16/MOSI, J5.pin3
  N6: Pro_Micro2.VCC, IC2.OUT, J2.pin2, J5.pin4
  N7: Pro_Micro2.GND#23, IC2.GND, J1.pin1, J2.pin1, J3.pin1, J4.pin1, LM2.pin4, C2.-, R4.Pin_0, J5.pin5
  N8: IC2.IN, F2.1, LM2.pin7, U3.Vin
  N9: F2.2, J1.pin2
  N10: J2.terminal_1, Grove2.GND
  N11: J2.terminal_2, Grove2.VCC
  N12: J2.terminal_3, Grove2.DIO
  N13: J2.terminal_4, Grove2.CLK
  N14: J3.terminal_1, S2.3
  N15: J3.terminal_2, S2.2
  N16: J4.pin2, J5.pin1
  N17: J4.terminal_1, M2.pin_1
  N18: J4.terminal_2, M2.pin_2
  N19: LM2.pin2, R4.Pin_1, R5.Pin_0
  N20: LM2.pin3, R2.Pin_0, C2.+
  N21: LM2.pin6, R5.Pin_1, R6.Pin_1, U3.ADJ
  N22: J5.pin2, R6.Pin_0, U3.Vout
  N23: J5.terminal_1, KY-2.NO
  N24: J5.terminal_2, KY-2.C
  N25: J5.terminal_3, KY-2.signal
  N26: J5.terminal_4, KY-2.power
  N27: J5.terminal_5, KY-2.ground

custom parts:
  Pro Micro: The SparkFun Pro Micro is a complete USB-based microcontoller development system, in a very small footprint, capable of implementing many types of projects. All programming can be done via the USB port.
  LM741: This is a single Op Amp DIP.
  Keyes Relay: The Keyes 5V relay module is suitable for SCM development, home appliance control. It uses a 5V~12V TIL control signal which can control DC / AC signal.
  Voltage Regulator: Voltage Regulator Standard LM317 adjustable voltage regulator. AOI (Adjust Output Input). Google 'LM317 Calculator' for easy to use app to get the two resistor values needed. 240/720 for 5V output. 240/390 for 3.3V output. Spark Fun Electronics SKU : COM-00527

// code stored in the sketch: TumblerController.h.ino
/**********************************
*                                                        *
*    Tumbler Motor Controller                *
*                                                       *
*        By Alon Fliess                            *
*                                                       *
*            2019                                    *
*                                                        *
/*********************************/

#ifndef _TUMBLER_CONTROLLER_H
#define _TUMBLER_CONTROLLER_H
// Module connection pins (Digital Pins)
#define CLK 2
#define DIO 3
#define SPD 6
#define BUTTON 5
#define RELAY 16

// The amount of time (in milliseconds) that a button action is conssidered
const unsigned int minimumButtonPressingTime = 75;
const unsigned int LongPressTime = 200;

const uint8_t SEG_DONE[] = {
  SEG_B | SEG_C | SEG_D | SEG_E | SEG_G,           // d
  SEG_A | SEG_B | SEG_C | SEG_D | SEG_E | SEG_F,   // O
  SEG_C | SEG_E | SEG_G,                           // n
  SEG_A | SEG_D | SEG_E | SEG_F | SEG_G            // E
  };

  const uint8_t SEG_START[] = {
  SEG_A | SEG_F | SEG_G | SEG_C | SEG_D,           // S
  SEG_B | SEG_G | SEG_C ,                          // t
  SEG_E | SEG_G,                                   // r
  SEG_B | SEG_G | SEG_C                            // t
  };

  const uint8_t SEG_STOP[] = {
  SEG_A | SEG_F | SEG_G | SEG_C | SEG_D,           // S
  SEG_B | SEG_G | SEG_C ,                          // t
  SEG_A | SEG_B | SEG_C | SEG_D | SEG_E | SEG_F,   // O
  SEG_A | SEG_F | SEG_G | SEG_B | SEG_E            // p
  };

  const uint8_t SEG_SPD[] = {
  0,                                               // _
  SEG_A | SEG_F | SEG_G | SEG_C | SEG_D,           // S
  SEG_A | SEG_F | SEG_G | SEG_B | SEG_E,           // p
  SEG_B | SEG_C | SEG_D | SEG_E | SEG_G            // d
  };

  const uint8_t SEG_SPD_DOWN[] = {
  SEG_G,                                           // -
  SEG_A | SEG_F | SEG_G | SEG_C | SEG_D,           // S
  SEG_A | SEG_F | SEG_G | SEG_B | SEG_E,           // p
  SEG_B | SEG_C | SEG_D | SEG_E | SEG_G            // d
  };

  const uint8_t SEG_DUR[] = {
  0,                                               // _
  SEG_B | SEG_C | SEG_D | SEG_E | SEG_G,           // d
  SEG_F | SEG_E | SEG_D | SEG_C | SEG_B,           // U
  SEG_E | SEG_G                                    // r
  };

  const uint8_t SEG_DUR_DOWN[] = {
  SEG_G,                                           // -
  SEG_B | SEG_C | SEG_D | SEG_E | SEG_G,           // d
  SEG_F | SEG_E | SEG_D | SEG_C | SEG_B,           // U
  SEG_E | SEG_G                                    // r
  };

  const uint8_t SEG_RESET[] = {
  SEG_E | SEG_G,                                   // r
  SEG_A | SEG_D | SEG_E | SEG_F | SEG_G,           // E
  SEG_A | SEG_F | SEG_G | SEG_C | SEG_D,           // S
  SEG_B | SEG_G | SEG_C                            // t
  };

const uint8_t PERIMETER[] = {4, 5, 0, 10, 20, 30, 31, 32, 33, 23, 13, 3};

typedef void (*func_t)();
class Action
{
  private:
  const uint8_t* _display;
  func_t _func;
  
  public:
  Action(const uint8_t* display, func_t func)
    : _display(display), _func(func) {}
  void Display();
  void Act();
};

enum ButtonAction {ButtonActionNone, ButtonActionShortPress, ButtonActionLongPress};

ButtonAction DetectButtonAction();

#endif //_TUMBLER_CONTROLLER_H

// code stored in the sketch: TumblerController.ino
/**********************************
*                                                        *
*    Tumbler Motor Controller                *
*                                                       *
*        By Alon Fliess                            *
*                                                       *
*            2019                                    *
*                                                        *
/*********************************/

#include <Arduino.h>
#include <TM1637Display.h>
#include "TumblerController.h"

TM1637Display display(CLK, DIO);
unsigned int speed = 3;
unsigned int time = 24 * 60; //in minutes
bool isRunning = false;
unsigned long lastAccountingTime;
unsigned long pressTime;
unsigned long buttonPressStartTime;
bool buttonPreviousState = false;
unsigned long lastActionTime = 0;
unsigned char currentAction = 0;

Action actions[] = {Action(SEG_START, &Start), 
                    Action(SEG_SPD, &SpeedUp), Action(SEG_SPD_DOWN, &SpeedDown),
                    Action(SEG_DUR, &TimeUp), Action(SEG_DUR_DOWN, &TimeDown),
                    Action(SEG_RESET, &Reset)
};

void DisplayRunningLoop(int times, int stepDelay)
{
  int length = sizeof(PERIMETER)/sizeof(PERIMETER[0]);
  for (int t = 0; t < times; ++t) //times
  {
    for (int loop = 0; loop < length; ++loop)
    {
      uint8_t LEDS[] = {0,0,0,0};
      for (int digit = 0; digit < length/2; ++digit)
      {
        int shiftedDigit = (digit + loop)%length;
        int index = PERIMETER[shiftedDigit] / 10;
        int led = 1 << (PERIMETER[shiftedDigit] % 10);
        LEDS[index] |= led;
      }
      display.setSegments(LEDS);
      delay(stepDelay);
    }
  }
}

void Start()
{
  isRunning = true;
  analogWrite(SPD, 75 + (speed - 1) * 30);
  delay(250);
  digitalWrite(RELAY, LOW);
  lastAccountingTime = millis();
}

void Stop()
{
  digitalWrite(RELAY, HIGH);
  digitalWrite(SPD, 0);
  isRunning = false;
  currentAction = 0; 
  DisplayRunningLoop(2, 4);
  display.clear();
  display.setSegments(SEG_STOP);
  delay(400);
  actions[currentAction].Display();
  lastActionTime = millis();  
}

void DisplaySpeed(bool shouldErase = true)
{
  if (shouldErase)
    display.clear();
  display.showNumberDec(speed, false); 
}

void SpeedUp()
{
  ++speed;
  if (speed > 5)
    speed = 5;
  DisplaySpeed();
}

void SpeedDown()
{
  --speed;
  if (speed < 1)
    speed = 1;
  DisplaySpeed();
}

void DisplayTime(bool shouldErase = true, uint8_t colon = 0b01000000)
{
  auto hours = time / 60;
  auto minutes = time % 60;
  if (shouldErase)
    display.clear();
  display.showNumberDecEx(minutes + hours * 100, colon, true);
}
void TimeUp()
{
  time += 30;
  DisplayTime();
}

void TimeDown()
{
  if (time == 0)
  return;
  
  if (time < 30)
  {
    --time;
    DisplayTime();
    return;
  }
  
  time -= 30;
  DisplayTime();
}

void Reset()
{
  speed = 3;
  isRunning = false;
  time = 24 * 60;
  DisplayRunningLoop(4, 2);
  currentAction = 0; 
  actions[currentAction].Display();
  lastActionTime = millis();
}

void Action::Display()
{
  display.clear();
  display.setSegments(_display);
}

void Action::Act()
{
  _func();
}


ButtonAction DetectButtonAction()
{
  bool current = digitalRead(BUTTON) == 0; //pull up
  if (!current && buttonPreviousState && (millis() - pressTime) > LongPressTime)
  {
    buttonPreviousState = false;
    Serial.println("ButtonActionLongPress");
    return ButtonActionLongPress;
  }
  //else
  if (!current && buttonPreviousState && (millis() - pressTime) > minimumButtonPressingTime)
  {
    buttonPreviousState = false;
    Serial.println("ButtonActionShortPress");
    return ButtonActionShortPress;
  }

  if (current && !buttonPreviousState)
  {
    pressTime = millis();
  }
  buttonPreviousState = current;
  return ButtonActionNone;
}

void setup()
{
  pinMode(SPD, OUTPUT);
  pinMode(BUTTON, INPUT_PULLUP); 
  digitalWrite(RELAY, HIGH);
  pinMode(RELAY, OUTPUT); 
  
 //blink 5 times
  display.clear();
  uint8_t data[] = { 0xff, 0xff, 0xff, 0xff };
  uint8_t blank[] = { 0x00, 0x00, 0x00, 0x00 };
  for (int i = 0; i < 5; ++i)
  {
    display.setBrightness(0x0f - 4 + i);
    display.setSegments(data);
    delay(25);
    display.setSegments(blank);
    delay(25);
  }
  display.clear();
  DisplayRunningLoop(4, 7);
  display.setSegments(SEG_START);
  Serial.begin(9600);
}

auto clockColon = 0b01000000;
byte lastSecondDigit = 0;
void HandleRunning(ButtonAction buttonAction)
{
  if (buttonAction != ButtonActionNone)
  {
    Stop();
    return;
  }
  bool shouldErase = false;
  if (millis() - lastAccountingTime >= 60000) //a minute
  {
    lastAccountingTime = millis();
    time -= 1;
    shouldErase = true;
  }

  byte secondDigit = (millis() / 1000)%10;
  if (secondDigit != lastSecondDigit) //a second has passed
  {
    lastSecondDigit = secondDigit;
    clockColon = (clockColon == 0b01000000) ? 0 : 0b01000000;
  }
  DisplayTime(shouldErase, clockColon);
  if (time == 0)
      Stop();
}

void ShowStatus()
{
    if ((millis() / 1000) % 2 == 1)
    {
      DisplayTime(false);
    }
    else
    {
      DisplaySpeed(false);
    }
}

void loop()
{
  if (millis() - lastActionTime > 5 * 60 * 1000)
    display.setBrightness(0);
    
  auto buttonAction = DetectButtonAction();
  if (isRunning)
  {
    HandleRunning(buttonAction);
    return;
  }
  //else
  display.setBrightness(0xf);
  //not running, handle menue
  if (buttonAction == ButtonActionLongPress)
  {
    currentAction = (currentAction + 1) % (sizeof(actions)/sizeof(actions[0]));
    actions[currentAction].Display();
    lastActionTime = millis();
    return;
  }
  //else
  if (buttonAction == ButtonActionShortPress)
  {
    actions[currentAction].Act();
    lastActionTime = millis();
  }

  if (millis() - lastActionTime > 10 * 1000)
  {
     ShowStatus();
  }
}
